# Fritzing sketch Lantern (saved by Fritzing 0.9.3b)
breadboards: 1

parts:
  Piezo_Element = Piezo Speaker
  1_Mohm = Resistor [tolerance=±5% resistance=1M package=THT]
  MCP602_Op_Amps = Dual Op-Amp [package=dip08]
  R1 = Resistor [tolerance=±5% resistance=330k package=THT]
  R2 = Resistor [tolerance=±5% resistance=10k package=THT]
  D1 = Rectifier Diode [part_number=1N4001 package="300 mil [THT]"]
  C1 = Tantalum Capacitor [capacitance=1μF package="100 mil [THT, tantalum]"]
  R3 = Resistor [tolerance=±5% resistance=470k package=THT]
  MCP602_Op_Amps1 = Dual Op-Amp [package=dip08]

nets:
  GND: Piezo_Element.pin1, 1_Mohm.Pin_0, MCP602_Op_Amps.A_V+, R2.Pin_0, C1.-, R3.Pin_1, MCP602_Op_Amps1.A_V+
  NonInv Amp (33x): Piezo_Element.pin2, 1_Mohm.Pin_1, MCP602_Op_Amps.A_+IN
  N1: MCP602_Op_Amps.A_OUT, R1.Pin_0, D1.anode
  N2: MCP602_Op_Amps.A_-IN, R1.Pin_1, R2.Pin_1
  5V: MCP602_Op_Amps.A_V-, MCP602_Op_Amps1.A_V-
  Percussive Envelope Detector: MCP602_Op_Amps.B_+IN, D1.cathode, C1.+, R3.Pin_0
  Buffer: MCP602_Op_Amps.B_-IN, MCP602_Op_Amps.B_OUT
